# Fritzing sketch final (saved by Fritzing 1.0.1rc)
circuit board: 8.46667cm x 5.64444cm
breadboards: 1

parts:
  RHT1 = Humidity and Temperature Sensor RHT03
  M1 = DC Motor [voltage_(max)=6V voltage_(min)=3V]
  J2 = Raspberry Pi Header 40pin [form="♂ (male)" package=THT]
  R2 = Resistor [tolerance=±5% power=0.25W resistance=220 package=THT]
  R1 = Resistor [tolerance=±5% resistance=220 package="0402 [SMD]"]
  Mod1 = Amica NodeMCU DEVKIT 1.0
  LED2 = LED - 5mm [color="Red (633nm)" current=0.030A package="5 mm [THT]"]
  IC1 = L293D [package=THT]
  R3 = Resistor [tolerance=±5% power=0.25W resistance=220 package=THT]
  J1 = Raspberry Pi Header 40pin [form="♂ (male)" package=THT]
  LED3 = LED - 5mm [color="Red (633nm)" current=0.030A package="5 mm [THT]"]
  VCC1 = Battery block 9V

nets (from the breadboard view):
  3V3: RHT1.Vcc, RHT1.Data-signal, RHT1.GND_2, J2.3v3, J2.3V3, R1.Pin_0
  N1: M1.pin_1, IC1.Out_2_(_Controlled_by_Enable_1_)
  N2: M1.pin_2, IC1.Out_1_(_Controlled_by_Enable_1_)
  N3: J2.GND, IC1.0V, VCC1.-
  N4: J2.GIPO17, IC1.In_2
  N5: J2.GIPO27, IC1.In_1
  N6: J2.GIPO22, IC1.Enable_1
  N7: J2.GIPO5, R1.Pin_1
  N8: R2.Pin_0, J1.GIPO12
  N9: R2.Pin_1, LED2.anode
  N10: Mod1.pin1, Mod1.pin_10, Mod1.pin_26, LED3.anode
  N11: Mod1.pin2, Mod1.pin_9, Mod1.pin_25, Mod1.pin_29, R3.Pin_0
  N12: Mod1.pin_16, R3.Pin_1, LED3.cathode
  N13: LED2.cathode, J1.GND
  N14: IC1.+V, VCC1.+

custom parts:
  Raspberry Pi Header 40pin: Raspberry Pi 40 pin header - for creating your own shields.
